// Logisim project fullthing.circ as structural Verilog: 13 circuits, main circuit main
module main (
);

  wire clock_1_out;
  wire [3:0] ALU1_zero;
  wire [7:0] A_reg_data_out, ALU1_out, bit_extender_1_out;

  Clock clock_1 (.out(clock_1_out));
  bus_register A_reg (.data_in(ALU1_out), .clock(clock_1_out), .data_out(A_reg_data_out));  // open: load
  Bit_Extender #(.in_width(1), .out_width(8)) bit_extender_1 (.out(bit_extender_1_out));  // open: in
  // AND_Gate and_1 has open pins: in0=A_reg_data_out, in1=bit_extender_1_out, out=open
  ALU ALU1 (
    .A(A_reg_data_out), .out(ALU1_out), .zero(ALU1_zero[0]), .overflow(ALU1_zero[1]), .carry(ALU1_zero[2]),
    .negative(ALU1_zero[3]));  // open: B, OP
  // Probe on ALU1_out
  // AND_Gate and_2 has open pins: in0={4'b0000, ALU1_zero}, out=open
endmodule

module ALU (
  input  [2:0] OP,
  input  [7:0] A,
  input  [7:0] B,
  output zero,
  output overflow,
  output carry,
  output negative,
  output [7:0] out
);

  wire [7:0] adder_subber_out, and_1_out, not_1_out, or_1_out, xor_1_out;

  ADD_SUB adder_subber (
    .A(A), .B(B), .op(OP[0]), .zero(zero), .negative(negative), .overflow(overflow), .carry(carry),
    .out(adder_subber_out));
  assign not_1_out = ~A;  // NOT_Gate not_1, 8 bits wide
  assign and_1_out = A & B;  // AND_Gate and_1, 8 bits wide
  assign or_1_out = A | B;  // OR_Gate or_1, 8 bits wide
  assign xor_1_out = A ^ B;  // XOR_Gate xor_1, 8 bits wide
  mux_8_bit_3 mux (
    .in_4(adder_subber_out), .in_5(adder_subber_out), .in_6(not_1_out), .in_7(and_1_out), .in_8(or_1_out),
    .in_9(xor_1_out), .in_10({1'b0, B[7:1]}), .in_11({B[6:0], 1'b0}), .in_1(OP[0]), .in_2(OP[1]),
    .in_3(OP[2]), .out_12(out));
endmodule

module full_adder (
  input  in_1,
  input  in_2,
  input  in_3,
  output out_4,
  output out_5
);

  wire and_1_out, and_2_out, xor_1_out;

  xor xor_1 (xor_1_out, in_1, in_2);
  xor xor_2 (out_4, xor_1_out, in_3);
  and and_1 (and_1_out, xor_1_out, in_3);
  and and_2 (and_2_out, in_1, in_2);
  or or_1 (out_5, and_1_out, and_2_out);
endmodule

module ADD_SUB (
  input  [7:0] B,
  input  op,
  input  [7:0] A,
  output zero,
  output [7:0] out,
  output negative,
  output overflow,
  output carry
);

  wire and_1_out, and_2_out, not_1_out, not_2_out, not_3_out;
  wire [7:0] xor_1_out;

  assign xor_1_out = B ^ {8{op}};  // XOR_Gate xor_1, 8 bits wide
  adder_8_bit full_adder_8_bit (
    .in_2(xor_1_out[0]), .in_3(xor_1_out[1]), .in_4(xor_1_out[2]), .in_5(xor_1_out[3]), .in_6(xor_1_out[4]),
    .in_7(xor_1_out[5]), .in_8(xor_1_out[6]), .in_9(xor_1_out[7]), .in_10(A[0]), .in_11(A[1]), .in_12(A[2]),
    .in_13(A[3]), .in_14(A[4]), .in_15(A[5]), .in_16(A[6]), .in_17(A[7]), .in_1(op), .out_18(out[0]),
    .out_19(out[1]), .out_20(out[2]), .out_21(out[3]), .out_22(out[4]), .out_23(out[5]), .out_24(out[6]),
    .out_25(negative), .out_26(carry));
  not not_1 (not_1_out, A[7]);
  not not_2 (not_2_out, negative);
  and and_1 (and_1_out, not_1_out, negative, not_3_out);
  not not_3 (not_3_out, xor_1_out[7]);
  and and_2 (and_2_out, A[7], not_2_out, xor_1_out[7]);
  nor nor_1 (zero, out[0], out[1], out[2], out[3], out[4], out[5], out[6], negative);
  or or_1 (overflow, and_1_out, and_2_out);

  assign out[7] = negative;
endmodule

module adder_8_bit (
  input  in_1,
  input  in_2,
  input  in_3,
  input  in_4,
  input  in_5,
  input  in_6,
  input  in_7,
  input  in_8,
  input  in_9,
  input  in_10,
  input  in_11,
  input  in_12,
  input  in_13,
  input  in_14,
  input  in_15,
  input  in_16,
  input  in_17,
  output out_18,
  output out_19,
  output out_20,
  output out_21,
  output out_22,
  output out_23,
  output out_24,
  output out_25,
  output out_26
);

  wire fulladder1_out_5, fulladder2_out_5, fulladder3_out_5, fulladder4_out_5, fulladder5_out_5,
       fulladder6_out_5, fulladder7_out_5;

  full_adder fulladder1 (.in_1(in_2), .in_2(in_10), .in_3(in_1), .out_4(out_18), .out_5(fulladder1_out_5));
  full_adder fulladder2 (.in_1(in_3), .in_2(in_11), .in_3(fulladder1_out_5), .out_4(out_19), .out_5(fulladder2_out_5));
  full_adder fulladder3 (.in_1(in_4), .in_2(in_12), .in_3(fulladder2_out_5), .out_4(out_20), .out_5(fulladder3_out_5));
  full_adder fulladder4 (.in_1(in_5), .in_2(in_13), .in_3(fulladder3_out_5), .out_4(out_21), .out_5(fulladder4_out_5));
  full_adder fulladder5 (.in_1(in_6), .in_2(in_14), .in_3(fulladder4_out_5), .out_4(out_22), .out_5(fulladder5_out_5));
  full_adder fulladder6 (.in_1(in_7), .in_2(in_15), .in_3(fulladder5_out_5), .out_4(out_23), .out_5(fulladder6_out_5));
  full_adder fulladder7 (.in_1(in_8), .in_2(in_16), .in_3(fulladder6_out_5), .out_4(out_24), .out_5(fulladder7_out_5));
  full_adder fulladder8 (.in_1(in_9), .in_2(in_17), .in_3(fulladder7_out_5), .out_4(out_25), .out_5(out_26));
endmodule

module mux (
  input  A,
  input  connector,
  input  B,
  output out_4
);

  wire and_1_out, and_2_out, nand_1_out;

  nand nand_1 (nand_1_out, A, connector);
  and and_1 (and_1_out, connector, B);
  and and_2 (and_2_out, A, nand_1_out);
  or or_1 (out_4, and_2_out, and_1_out);
endmodule

module mux_8_bit (
  input  in_1,
  input  [7:0] in_2,
  input  [7:0] in_3,
  output [7:0] out_4
);

  mux mux1 (.A(in_2[0]), .connector(in_1), .B(in_3[0]), .out_4(out_4[0]));
  mux mux2 (.A(in_2[1]), .connector(in_1), .B(in_3[1]), .out_4(out_4[1]));
  mux mux3 (.A(in_2[2]), .connector(in_1), .B(in_3[2]), .out_4(out_4[2]));
  mux mux4 (.A(in_2[3]), .connector(in_1), .B(in_3[3]), .out_4(out_4[3]));
  mux mux5 (.A(in_2[4]), .connector(in_1), .B(in_3[4]), .out_4(out_4[4]));
  mux mux6 (.A(in_2[5]), .connector(in_1), .B(in_3[5]), .out_4(out_4[5]));
  mux mux7 (.A(in_2[6]), .connector(in_1), .B(in_3[6]), .out_4(out_4[6]));
  mux mux8 (.A(in_2[7]), .connector(in_1), .B(in_3[7]), .out_4(out_4[7]));
endmodule

module mux_8_bit_2 (
  input  in_1,
  input  in_2,
  input  [7:0] in_3,
  input  [7:0] in_4,
  input  [7:0] in_5,
  input  [7:0] in_6,
  output [7:0] out_7
);

  wire [7:0] mux1_out_4, mux3_out_4;

  mux_8_bit mux1 (.in_2(in_3), .in_3(in_4), .in_1(in_1), .out_4(mux1_out_4));
  mux_8_bit mux3 (.in_2(in_5), .in_3(in_6), .in_1(in_1), .out_4(mux3_out_4));
  mux_8_bit mux2 (.in_2(mux1_out_4), .in_3(mux3_out_4), .in_1(in_2), .out_4(out_7));
endmodule

module mux_8_bit_3 (
  input  in_1,
  input  in_2,
  input  in_3,
  input  [7:0] in_4,
  input  [7:0] in_5,
  input  [7:0] in_6,
  input  [7:0] in_7,
  input  [7:0] in_8,
  input  [7:0] in_9,
  input  [7:0] in_10,
  input  [7:0] in_11,
  output [7:0] out_12
);

  wire [7:0] mux1_out_7, mux3_out_7;

  mux_8_bit_2 mux1 (.in_3(in_4), .in_4(in_5), .in_5(in_6), .in_6(in_7), .in_1(in_1), .in_2(in_2), .out_7(mux1_out_7));
  mux_8_bit_2 mux3 (.in_3(in_8), .in_4(in_9), .in_5(in_10), .in_6(in_11), .in_1(in_1), .in_2(in_2), .out_7(mux3_out_7));
  mux_8_bit mux2 (.in_2(mux1_out_7), .in_3(mux3_out_7), .in_1(in_3), .out_4(out_12));
endmodule

module latch1 (
  input  in_1,
  input  in_2,
  output out_3,
  output out_4
);

  wire nand_1_out, nand_2_out, not_1_out;

  not not_1 (not_1_out, in_1);
  nand nand_1 (nand_1_out, in_1, in_2);
  nand nand_2 (nand_2_out, in_2, not_1_out);
  nor nor_1 (out_3, nand_1_out, out_4);
  nor nor_2 (out_4, out_3, nand_2_out);
endmodule

module pulse_d_flipflop (
  input  value,
  input  enable,
  output Q,
  output QB
);

  wire buffer_1_out, nand_1_out, nand_2_out, nand_3_out, not_1_out, not_2_out, not_3_out;

  buf buffer_1 (buffer_1_out, enable);
  not not_1 (not_1_out, buffer_1_out);
  nand nand_1 (nand_1_out, enable, not_1_out);
  not not_2 (not_2_out, nand_1_out);
  not not_3 (not_3_out, value);
  nand nand_2 (nand_2_out, value, not_2_out);
  nand nand_3 (nand_3_out, not_2_out, not_3_out);
  nand nand_4 (Q, nand_2_out, QB);
  nand nand_5 (QB, Q, nand_3_out);
endmodule

module bus_register (
  input  [7:0] data_in,
  input  load,
  input  clock,
  output [7:0] data_out
);

  wire and_1_out;
  wire [7:0] pulse_d_flipflop_8_q;

  and and_1 (and_1_out, load, clock);
  pulse_d_flipflop pulse_d_flipflop_1 (
    .value(data_in[7]), .enable(and_1_out), .Q(pulse_d_flipflop_8_q[7]));  // open: QB
  pulse_d_flipflop pulse_d_flipflop_2 (
    .value(data_in[6]), .enable(and_1_out), .Q(pulse_d_flipflop_8_q[6]));  // open: QB
  pulse_d_flipflop pulse_d_flipflop_3 (
    .value(data_in[5]), .enable(and_1_out), .Q(pulse_d_flipflop_8_q[5]));  // open: QB
  pulse_d_flipflop pulse_d_flipflop_4 (
    .value(data_in[4]), .enable(and_1_out), .Q(pulse_d_flipflop_8_q[4]));  // open: QB
  pulse_d_flipflop pulse_d_flipflop_5 (
    .value(data_in[3]), .enable(and_1_out), .Q(pulse_d_flipflop_8_q[3]));  // open: QB
  pulse_d_flipflop pulse_d_flipflop_6 (
    .value(data_in[2]), .enable(and_1_out), .Q(pulse_d_flipflop_8_q[2]));  // open: QB
  pulse_d_flipflop pulse_d_flipflop_7 (
    .value(data_in[1]), .enable(and_1_out), .Q(pulse_d_flipflop_8_q[1]));  // open: QB
  pulse_d_flipflop pulse_d_flipflop_8 (
    .value(data_in[0]), .enable(and_1_out), .Q(pulse_d_flipflop_8_q[0]));  // open: QB
  assign data_out = pulse_d_flipflop_8_q;  // Buffer buffer_1, 8 bits wide
endmodule

module enable_register (
  input  [7:0] data_in,
  input  load,
  input  clock,
  input  enable,
  output [7:0] data_out
);

  wire [7:0] bus_register_1_data_out;

  assign data_out = {8{enable}} & bus_register_1_data_out;  // AND_Gate and_1, 8 bits wide
  bus_register bus_register_1 (.data_in(data_in), .load(load), .clock(clock), .data_out(bus_register_1_data_out));
endmodule
