// Logisim project registers.circ as structural Verilog
module latch1 (
  input  in_1,
  input  in_2,
  output out_3,
  output out_4
);

  wire nand_1_out, nand_2_out, not_1_out;

  not not_1 (not_1_out, in_1);
  nand nand_1 (nand_1_out, in_1, in_2);
  nand nand_2 (nand_2_out, in_2, not_1_out);
  nor nor_1 (out_3, nand_1_out, out_4);
  nor nor_2 (out_4, out_3, nand_2_out);
endmodule

module pulse_d_flipflop (
  input  in_1,
  input  in_2,
  output out_3,
  output out_4
);

  wire and_1_out, buffer_1_out, nand_1_out, nand_2_out, not_1_out, not_2_out;

  buf buffer_1 (buffer_1_out, in_2);
  not not_1 (not_1_out, buffer_1_out);
  and and_1 (and_1_out, in_2, not_1_out);
  not not_2 (not_2_out, in_1);
  nand nand_1 (nand_1_out, in_1, and_1_out);
  nand nand_2 (nand_2_out, and_1_out, not_2_out);
  nand nand_3 (out_3, nand_1_out, out_4);
  nand nand_4 (out_4, out_3, nand_2_out);
endmodule
